# Fritzing sketch obd-logger-schematic-v1 (saved by Fritzing 1.0.8)

parts:
  Micro_SD_Card_Module = MicroSD Card Module
  Microcontroller = Arduino Nano (Rev3.0) (ICSP)
  OBD2_Adapter_(5V) = Header 4 [package=molex-1x4_lock]
  I2C_Display = Grove OLED 128x96

nets:
  GND: Micro_SD_Card_Module.GND, Microcontroller.GND, OBD2_Adapter_(5V).2, I2C_Display.GND
  VCC: Micro_SD_Card_Module.VCC, Microcontroller.5V, OBD2_Adapter_(5V).1
  N1: Micro_SD_Card_Module.MISO, Microcontroller.D12/MISO
  N2: Micro_SD_Card_Module.MOSI, Microcontroller.D11/MOSI
  N3: Micro_SD_Card_Module.SCK, Microcontroller.D13/SCK
  N4: Micro_SD_Card_Module.CS, Microcontroller.D10
  N5: Microcontroller.D1/TX, OBD2_Adapter_(5V).4
  N6: Microcontroller.D0/RX, OBD2_Adapter_(5V).3
  N7: Microcontroller.A5, I2C_Display.SCL
  N8: Microcontroller.A4, I2C_Display.SDA
  3V3: Microcontroller.3V3, I2C_Display.VCC
